// Logisim project input.circ as structural Verilog: 1 circuit, main circuit main
module main (
  input  [1:0] Direction,
  input  [1:0] in_2
);

  wire Runway_Picker_out_5, Runway_Picker_out_6, Runway_status_runway_a_status,
       Runway_status_runway_b_status, undriven, undriven_2;
  wire [1:0] bitadder_1_out;

  runway_picker_main Runway_Picker (
    .Direction_1(Direction[0]), .Direction_2(Direction[1]), .Runway_A_status(undriven),
    .Runway_B_status(undriven_2), .out_5(Runway_Picker_out_5), .out_6(Runway_Picker_out_6));
  runway_status_main Runway_status (
    .Runway_B_status(Runway_status_runway_b_status), .Runway_A_status(Runway_status_runway_a_status),
    .Chosen_Runway(in_2));
  BitAdder #(.width(1)) bitadder_1 (.in0(Runway_Picker_out_5), .in1(Runway_Picker_out_6), .out(bitadder_1_out));
endmodule
